# Fritzing sketch rpi_lcd (saved by Fritzing 0.9.3b)
breadboards: 1

parts:
  U1 = LCD-16X2 [package=lcd-16x2]
  MCU1 = Raspberry Pi Zero W
  R1 = TRIMPOT [package=trim_pot_pth]
  S1 = Pushbutton [package=THT]
  S2 = Pushbutton [package=THT]
  S3 = Pushbutton [package=THT]

nets:
  GND: U1.VSS, U1.R_W, U1.K, MCU1.pin_9, MCU1.pin_30, R1.CW, S1.leg1, S2.leg1, S3.leg0
  5V: U1.VDD, U1.A, MCU1.pin_2, R1.CCW
  N1: U1.VO, R1.WIPER
  N2: U1.RS, MCU1.pin_13
  N3: U1.E, MCU1.pin_15
  N4: U1.DB4, MCU1.pin_22
  N5: U1.DB5, MCU1.pin_18
  N6: U1.DB6, MCU1.pin_16
  N7: U1.DB7, MCU1.pin_12
  N8: MCU1.pin_5, S3.leg1
  N9: MCU1.pin_32, S2.leg0
  N10: MCU1.pin_37, S1.leg0

custom parts:
  Raspberry Pi Zero W: The Raspberry Pi Zero is half the size of a Model A+, with twice the utility. A tiny Raspberry Pi that’s affordable enough for any project! · 1Ghz, Single-core CPU · 512MB RAM · Mini HDMI and USB On-The-Go ports · Micro USB power · HAT-compatible 40-pin header. Jan 2018: In this version schematic has been changed so the pins match the GPIO connector. I.e. the left hand pins are all the pins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
