# Fritzing sketch trinket with switch and leds (saved by Fritzing 0.9.3b)
breadboards: 1

parts:
  Part1 = Adafruit Trinket 5V
  S1 = SPST Switch [package=switch-spdt-smd]
  LED1 = smd LED [color="White (6500K)" package="0603 [SMD]"]
  Q1 = NPN-Transistor [package="SOT-23 [SMD]"]
  Q2 = NPN-Transistor [package="SOT-23 [SMD]"]
  LED2 = smd LED [color="White (6500K)" package="0603 [SMD]"]
  LED3 = smd LED [color="White (6500K)" package="0603 [SMD]"]
  R1 = Resistor [tolerance=±5% resistance=220 package="2512 [SMD]"]
  R2 = Resistor [tolerance=±5% resistance=220 package="2512 [SMD]"]
  R3 = Resistor [tolerance=±5% resistance=220 package="2512 [SMD]"]

nets:
  N1: Part1.VBAT, LED1.cathode
  GND: Part1.GND, S1.S, Q1.2, Q2.2
  N2: Part1.#1, Q1.0
  N3: Part1.#0, Q2.0
  N4: S1.O, R1.Pin_0
  12V: S1.P, R2.Pin_0, R3.Pin_0
  N5: LED1.anode, R1.Pin_1
  N6: Q1.1, LED2.cathode
  N7: Q2.1, LED3.cathode
  N8: LED2.anode, R2.Pin_1
  N9: LED3.anode, R3.Pin_1

custom parts:
  Adafruit Trinket 5V: Trinket may be small, but do not be fooled by its size! It's a tiny microcontroller board, built around the Atmel ATtiny85, a little chip with a lot of power. We wanted to design a microcontroller board that was small enough to fit into any project, and low cost enough to use without hesitation. Perfect for when you don't want to give up your expensive dev-board and you aren't willing to take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
