# Fritzing sketch rpi and display (saved by Fritzing 0.9.3b)
breadboards: 1

parts:
  U1 = LCD-16X2 [package=lcd-8x2-kit]
  U2 = POT [package=alps_pot]
  S1 = Round Pushbutton
  S2 = Round Pushbutton
  MCU1 = Raspberry Pi Zero W

nets:
  GND: U1.VSS, U1.R_W, U1.DB4, U1.K, U2.A, S1.leg0, S2.leg0, MCU1.pin_9, MCU1.pin_25, MCU1.pin_39
  5V: U1.VDD, U1.A, U2.E, MCU1.pin_2, MCU1.pin_4
  N1: U1.VO, U2.S
  N2: U1.RS, MCU1.pin_27
  N3: U1.E, MCU1.pin_22
  N4: U1.DB5, MCU1.pin_24
  N5: U1.DB6, MCU1.pin_23
  N6: U1.DB7, MCU1.pin_18
  N7: S1.leg1, MCU1.pin_26
  N8: S2.leg1, MCU1.pin_12

custom parts:
  Raspberry Pi Zero W: The Raspberry Pi Zero is half the size of a Model A+, with twice the utility. A tiny Raspberry Pi that’s affordable enough for any project! · 1Ghz, Single-core CPU · 512MB RAM · Mini HDMI and USB On-The-Go ports · Micro USB power · HAT-compatible 40-pin header. Jan 2018: In this version schematic has been changed so the pins match the GPIO connector. I.e. the left hand pins are all the pins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
